# Fritzing sketch zero-g-fountain (saved by Fritzing 0.9.3b)

parts:
  M1 = DC Motor
  Part1 = SparkFun ESP8266 Thing
  NEOPIXEL1 = Neopixel Strip -- White (60/m)
  R1 = Resistor [tolerance=±5% resistance=470 package=THT]
  S1 = H-Bridge with L298N
  HLK-PM2 = HLK-PM12 [part_number=HLK-PM12]
  M2 = RioRand LM2596

nets:
  N1: M1.pin_1, S1.M2-02
  N2: M1.pin_2, S1.M2-01
  N3: Part1.GPIO0, S1.IN3
  N4: Part1.GPIO4, S1.IN4
  N5: Part1.GPIO13, S1.ENB
  N6: Part1.GPIO12, R1.Pin_0
  N7: NEOPIXEL1.+5V, M2.Pin_3
  N8: NEOPIXEL1.DI, R1.Pin_1
  N9: NEOPIXEL1.GND, M2.Pin_4
  N10: S1.12V, HLK-PM2.+Vo, M2.Pin_1
  N11: S1.GND, HLK-PM2.-Vo, M2.Pin_2

notes:
  enA needs to be PWM
  Use this converter only for up to 2A (maybe 3A with heatsink)
  230V to 12V converter, Ampere depending on the amount of your LEDs

custom parts:
  Neopixel Strip -- White (60/m): Neopixel Strip, White, 60 pixels per meter.
  H-Bridge with L298N: h-bridge
